# Fritzing sketch inthebox_yun (saved by Fritzing 0.9.3b)
breadboards: 1

parts:
  Door_Opened_Sensor = hc-sr04
  VCC1 = Battery block 9V
  R2 = Resistor [tolerance=±5% resistance=1k package="1206 [SMD]"]
  RFID_Buzzer = Piezo Speaker
  RFID_Door_Lock = RFID-RC522-v2
  LED_RFID_State = RGB LED (com. cathode, rbg) [package="5 mm [THT]"]
  R3 = Resistor [tolerance=±5% resistance=1k package="1206 [SMD]"]
  micro-controller = Arduino Yun
  Weight_Sensor = Basic Force Sensing Resistor (FSR) [package=THT]

nets:
  VCC: Door_Opened_Sensor.VCC, micro-controller.5V, Weight_Sensor.pin_0
  N1: Door_Opened_Sensor.Trig, micro-controller.D3_PWM
  N2: Door_Opened_Sensor.Echo, micro-controller.D2
  GND: Door_Opened_Sensor.GND, VCC1.-, RFID_Buzzer.pin1, R3.Pin_0, micro-controller.GND
  N3: VCC1.+, micro-controller.VIN
  N4: R2.Pin_0, micro-controller.RESET
  N5: R2.Pin_1, micro-controller.D13/SCK
  N6: RFID_Buzzer.pin2, micro-controller.D12/MISO
  N7: RFID_Door_Lock.SDA, micro-controller.D11_PWM/MOSI
  N8: RFID_Door_Lock.SCK, micro-controller.D10_PWM/SS
  N9: RFID_Door_Lock.MOSI, micro-controller.D9_PWM
  N10: RFID_Door_Lock.MISO, micro-controller.D8
  N11: RFID_Door_Lock.GND, LED_RFID_State.common_cathode
  N12: RFID_Door_Lock.RST, micro-controller.D7
  3.3V: RFID_Door_Lock.3.3V, micro-controller.3V3
  N13: LED_RFID_State.red_anode, micro-controller.D6_PWM
  N14: LED_RFID_State.blue_anode, micro-controller.D5_PWM
  N15: LED_RFID_State.green_anode, micro-controller.D4
  N16: R3.Pin_1, micro-controller.A1, Weight_Sensor.pin_1

custom parts:
  RFID-RC522-v2: A simple China made RFID-RC522 Reader; do check the pin labels, as this is a MFRC522 based clone.
